// Logisim project control-logic.circ as structural Verilog: 1 circuit, main circuit control_logic
module control_logic (
  input  [31:0] Instruction,
  input  BrEq,
  input  BrLt,
  output PCSel,
  output RegWEn,
  output [2:0] ImmSel,
  output BrUn,
  output ASel,
  output BSel,
  output [3:0] ALUSel,
  output MemWEn,
  output [1:0] WBSel
);

  wire add0, addi15, and11, and_17_out, and_18_out, and_19_out, and_20_out, andi22, auipc32, beq26, BFormat,
       bge29, bgeu31, blt28, bltu30, bne27, comparator_1_eq, comparator_2_eq, demultiplexer_1_out0,
       demultiplexer_1_out1, demultiplexer_1_out2, demultiplexer_1_out3, demultiplexer_1_out4,
       demultiplexer_1_out5, demultiplexer_1_out6, demultiplexer_1_out7, demultiplexer_4_out1,
       demultiplexer_4_out5, f7is0, f7is1, f7is20, IFormatLoad, IFormatR, jal34, jalr35, lb12, lh13, lui33,
       lw14, mul1, mulh4, mulhu5, not_1_out, not_2_out, or10, or_1_out, or_2_out, or_3_out, or_4_out,
       or_5_out, or_6_out, ori21, RFormat, sb23, SFormat, sh24, sll3, slli16, slt6, slti17, sra9, srai20,
       srl8, srli19, sub2, sw25, xor7, xori18;
  wire [5:0] ROMInput;
  wire [15:14] rom_1_data;

  Comparator #(.width(3)) comparator_1 (.a(Instruction[14:12]), .b(3'b000), .eq(comparator_1_eq));  // open: gt, lt
  and and_1 (jalr35, comparator_1_eq, comparator_2_eq);
  Comparator #(.width(7)) comparator_2 (.a(Instruction[6:0]), .b(7'b1100111), .eq(comparator_2_eq));  // open: gt, lt
  Comparator #(.width(7)) comparator_3 (.a(Instruction[6:0]), .b(7'b0100011), .eq(SFormat));  // open: gt, lt
  Comparator #(.width(7)) comparator_4 (.a(Instruction[6:0]), .b(7'b0110011), .eq(RFormat));  // open: gt, lt
  Demultiplexer #(.select(3)) demultiplexer_1 (
    .out0(demultiplexer_1_out0), .out1(demultiplexer_1_out1), .out2(demultiplexer_1_out2),
    .out3(demultiplexer_1_out3), .out4(demultiplexer_1_out4), .out5(demultiplexer_1_out5),
    .out6(demultiplexer_1_out6), .out7(demultiplexer_1_out7), .in(RFormat), .sel(Instruction[14:12]));
  Demultiplexer #(.select(3)) demultiplexer_2 (
    .out0(sb23), .out1(sh24), .out2(sw25), .in(SFormat), .sel(Instruction[14:12]));  // open: out3, out4, out5, out6, out7
  ROM #(.addrWidth(6), .dataWidth(16)) rom_1 (
    .addr(ROMInput), .data({rom_1_data, WBSel, MemWEn, ALUSel, BSel, ASel, BrUn, ImmSel, RegWEn}));
  and and_2 (mul1, f7is1, demultiplexer_1_out0);
  and and_3 (sub2, f7is20, demultiplexer_1_out0);
  and and_4 (add0, f7is0, demultiplexer_1_out0);
  and and_5 (mulh4, f7is1, demultiplexer_1_out1);
  and and_6 (sll3, f7is0, demultiplexer_1_out1);
  and and_7 (slt6, f7is0, demultiplexer_1_out2);
  and and_8 (mulhu5, f7is1, demultiplexer_1_out3);
  and and_9 (xor7, demultiplexer_1_out4, f7is0);
  and and_10 (srl8, demultiplexer_1_out5, f7is0);
  and and_11 (sra9, demultiplexer_1_out5, f7is20);
  and and_12 (or10, demultiplexer_1_out6, f7is0);
  and and_13 (and11, demultiplexer_1_out7, f7is0);
  Comparator #(.width(7)) comparator_5 (.a(Instruction[6:0]), .b(7'b1101111), .eq(jal34));  // open: gt, lt
  Comparator #(.width(7)) comparator_6 (.a(Instruction[6:0]), .b(7'b1100011), .eq(BFormat));  // open: gt, lt
  Comparator #(.width(7)) comparator_7 (.a(Instruction[6:0]), .b(7'b0000011), .eq(IFormatLoad));  // open: gt, lt
  Comparator #(.width(7)) comparator_8 (.a(Instruction[31:25]), .b({7{1'b0}}), .eq(f7is0));  // open: gt, lt
  Comparator #(.width(7)) comparator_9 (.a(Instruction[31:25]), .b(7'b0000001), .eq(f7is1));  // open: gt, lt
  Demultiplexer #(.select(3)) demultiplexer_3 (
    .out0(lb12), .out1(lh13), .out2(lw14), .in(IFormatLoad), .sel(Instruction[14:12]));  // open: out3, out4, out5, out6, out7
  Demultiplexer #(.select(3)) demultiplexer_4 (
    .out0(addi15), .out1(demultiplexer_4_out1), .out2(slti17), .out4(xori18), .out5(demultiplexer_4_out5),
    .out6(ori21), .out7(andi22), .in(IFormatR), .sel(Instruction[14:12]));  // open: out3
  Demultiplexer #(.select(3)) demultiplexer_5 (
    .out0(beq26), .out1(bne27), .out4(blt28), .out5(bge29), .out6(bltu30), .out7(bgeu31), .in(BFormat),
    .sel(Instruction[14:12]));  // open: out2, out3
  Comparator #(.width(7)) comparator_10 (.a(Instruction[31:25]), .b(7'b0100000), .eq(f7is20));  // open: gt, lt
  Comparator #(.width(7)) comparator_11 (.a(Instruction[6:0]), .b(7'b0110111), .eq(lui33));  // open: gt, lt
  Comparator #(.width(7)) comparator_12 (.a(Instruction[6:0]), .b(7'b0010111), .eq(auipc32));  // open: gt, lt
  Comparator #(.width(7)) comparator_13 (.a(Instruction[6:0]), .b(7'b0010011), .eq(IFormatR));  // open: gt, lt
  and and_14 (slli16, f7is0, demultiplexer_4_out1);
  and and_15 (srli19, demultiplexer_4_out5, f7is0);
  and and_16 (srai20, demultiplexer_4_out5, f7is20);
  // Priority_Encoder #(.select_enc(6)) priority_encoder_1: pin names not known; wires that end beside it: ROMInput, add0, mul1, sub2, sll3, mulh4, mulhu5, slt6, xor7, srl8, sra9, or10, and11, lb12, lh13, lw14, addi15, slli16, slti17, xori18, srli19, srai20, ori21, andi22, sb23, sh24, sw25, beq26, bne27, blt28, bge29, bltu30, bgeu31, auipc32, lui33, jal34, jalr35
  not not_1 (not_1_out, BrEq);
  or or_1 (or_1_out, blt28, bltu30);
  or or_2 (or_2_out, bge29, bgeu31);
  not not_2 (not_2_out, BrLt);
  and and_17 (and_17_out, beq26, BrEq);
  and and_18 (and_18_out, bne27, not_1_out);
  and and_19 (and_19_out, or_1_out, BrLt);
  and and_20 (and_20_out, or_2_out, not_2_out);
  or or_3 (or_3_out, jal34, jalr35);
  or or_4 (or_4_out, and_17_out, and_18_out);
  or or_5 (or_5_out, and_19_out, and_20_out);
  or or_6 (or_6_out, or_5_out, or_3_out);
  or or_7 (PCSel, or_4_out, or_6_out);

  // Other names for the same wires on the sheet: opcode[6:0] = Instruction[6:0]; funct3[2:0] = Instruction[14:12];
  //   funct7[6:0] = Instruction[31:25]

  // Notes on the sheet:
  //   INPUTS to your circuit
  //   Connect ROM Input here ->
  //   contents of rom_1 (hex, n*v repeats v):
  //   1001 1401 1601 1081 1481 1581 1101 1201 1281 1681 1301 1381 41 41 41 1041 10c1 1141 1241 12c1 16c1
  //   1341 13c1 842 842 842 4*64 74 74 1047 17c7 2069 2041
  //   ROM FOR CONTROL LOGIC
  //   DON'T CHANGE THE LOCATIONS OF THE INPUTS AND OUTPUTS!
  //   This is only if you choose to do the ROM option
  //   CONNECT
  //   WIRE
  //   TO
  //   USE
  //   ROM
  //   OUTPUT from your circuit
  //   Reminder: If using ROM, use combinational logic for PCSel
endmodule
