// Logisim project imm-gen.circ as structural Verilog: 1 circuit, main circuit imm_gen
module imm_gen (
  input  [31:0] Instruction,
  input  [2:0] ImmSel,
  output [31:0] Immediate
);

  wire [7:0] s1;
  wire [9:0] s2;
  wire [31:0] bit_extender_1_out, bit_extender_2_out, bit_extender_3_out, bit_extender_4_out,
       demultiplexer_1_out0, demultiplexer_1_out1, demultiplexer_1_out2, demultiplexer_1_out3,
       demultiplexer_1_out4;

  Demultiplexer #(.select(3), .width(32)) demultiplexer_1 (
    .out0(demultiplexer_1_out0), .out1(demultiplexer_1_out1), .out2(demultiplexer_1_out2),
    .out3(demultiplexer_1_out3),
    .out4({demultiplexer_1_out4[31], s2, demultiplexer_1_out4[20], s1, demultiplexer_1_out4[11:0]}),
    .in(Instruction), .sel(ImmSel));  // open: out5, out6, out7
  assign bit_extender_1_out = {{20{demultiplexer_1_out0[31]}}, demultiplexer_1_out0[31:20]};  // Bit_Extender bit_extender_1
  assign bit_extender_2_out = {{20{demultiplexer_1_out1[31]}}, {demultiplexer_1_out1[31:25], demultiplexer_1_out1[11:7]}};  // Bit_Extender bit_extender_2
  assign bit_extender_3_out = {{19{demultiplexer_1_out2[31]}}, {demultiplexer_1_out2[31], demultiplexer_1_out2[7], demultiplexer_1_out2[30:25], demultiplexer_1_out2[11:8], 1'b0}};  // Bit_Extender bit_extender_3
  assign bit_extender_4_out = {{11{demultiplexer_1_out4[31]}}, {demultiplexer_1_out4[31], s1, demultiplexer_1_out4[20], s2, 1'b0}};  // Bit_Extender bit_extender_4
  Multiplexer #(.select(3), .width(32)) multiplexer_1 (
    .in0(bit_extender_1_out), .in1(bit_extender_2_out), .in2(bit_extender_3_out),
    .in3({demultiplexer_1_out3[31:12], {12{1'b0}}}), .in4(bit_extender_4_out), .out(Immediate), .sel(ImmSel));  // open: in5, in6, in7

  // Notes on the sheet:
  //   INPUTS to your circuit
  //   DON'T CHANGE THE LOCATIONS OF THE INPUTS AND OUTPUTS!
  //   OUTPUT from your circuit
endmodule
