// Logisim project partial-load.circ as structural Verilog: 1 circuit, main circuit partial_load
module partial_load (
  input  [31:0] Instruction,
  input  [31:0] MemAddress,
  input  [31:0] DataFromMem,
  output [31:0] DataToReg
);

  wire IFormatLoad, lb, lh, lw;
  wire [1:0] demultiplexer_2_out0, demultiplexer_2_out1, demultiplexer_2_out2, loadInstruction;
  wire [7:0] multiplexer_1_out;
  wire [15:0] multiplexer_3_out;
  wire [31:0] bit_extender_1_out, bit_extender_2_out, multiplexer_2_out;

  Comparator #(.width(7)) comparator_1 (.a(Instruction[6:0]), .b(7'b0000011), .eq(IFormatLoad));  // open: gt, lt
  Demultiplexer #(.select(3)) demultiplexer_1 (
    .out0(lb), .out1(lh), .out2(lw), .in(IFormatLoad), .sel(Instruction[14:12]));  // open: out3, out4, out5, out6, out7
  Priority_Encoder #(.select_enc(2)) priority_encoder_1 (
    .in0(lb), .in1(lh), .in2(lw), .out(loadInstruction));  // open: in3, gs, en_out, en_in
  Demultiplexer #(.select(2), .width(2)) demultiplexer_2 (
    .out0(demultiplexer_2_out0), .out1(demultiplexer_2_out1), .out2(demultiplexer_2_out2),
    .in(MemAddress[1:0]), .sel(loadInstruction));  // open: out3
  Multiplexer #(.select(2), .width(8)) multiplexer_1 (
    .in0(DataFromMem[7:0]), .in1(DataFromMem[15:8]), .in2(DataFromMem[23:16]), .in3(DataFromMem[31:24]),
    .out(multiplexer_1_out), .sel(demultiplexer_2_out0));
  assign bit_extender_1_out = {{24{multiplexer_1_out[7]}}, multiplexer_1_out};  // Bit_Extender bit_extender_1
  Multiplexer #(.select(2), .width(32)) multiplexer_2 (
    .in0(DataFromMem), .out(multiplexer_2_out), .sel(demultiplexer_2_out2));  // open: in1, in2, in3
  assign bit_extender_2_out = {{16{multiplexer_3_out[15]}}, multiplexer_3_out};  // Bit_Extender bit_extender_2
  Multiplexer #(.select(2), .width(16)) multiplexer_3 (
    .in0(DataFromMem[15:0]), .in1(DataFromMem[23:8]), .in2(DataFromMem[31:16]), .out(multiplexer_3_out),
    .sel(demultiplexer_2_out1));  // open: in3
  Multiplexer #(.select(2), .width(32)) multiplexer_4 (
    .in0(bit_extender_1_out), .in1(bit_extender_2_out), .in2(multiplexer_2_out), .out(DataToReg),
    .sel(loadInstruction));  // open: in3

  // Other names for the same wires on the sheet: data1[7:0] = DataFromMem[7:0]; data2[7:0] = DataFromMem[15:8];
  //   data3[7:0] = DataFromMem[23:16]; data4[7:0] = DataFromMem[31:24]; opcode[6:0] = Instruction[6:0];
  //   funct3[2:0] = Instruction[14:12]; funct7[6:0] = Instruction[31:25]; lowadr[1:0] = MemAddress[1:0]

  // Notes on the sheet:
  //   INPUTS to your circuit
  //   DON'T CHANGE THE LOCATIONS OF THE INPUTS AND OUTPUTS!
  //   OUTPUT from your circuit
endmodule
