// Logisim project partial-store.circ as structural Verilog: 1 circuit, main circuit partial_store
module partial_store (
  input  [31:0] Instruction,
  input  [31:0] MemAddress,
  input  [31:0] DataFromReg,
  input  MemWEn,
  output [3:0] MemWriteMask,
  output [31:0] DataToMem
);

  wire NotStore, sb, SFormat, sh, sw;
  wire [1:0] demultiplexer_2_out0, demultiplexer_2_out1, demultiplexer_2_out2, demultiplexer_3_out0,
       demultiplexer_3_out1, demultiplexer_3_out2, storeInstruction;
  wire [3:0] multiplexer_2_out, multiplexer_3_out, multiplexer_4_out;
  wire [7:0] demultiplexer_4_out0, demultiplexer_4_out1, demultiplexer_4_out2, demultiplexer_4_out3;
  wire [15:0] demultiplexer_5_out0;
  wire [31:0] demultiplexer_6_out0, multiplexer_6_out, multiplexer_7_out;
  wire [31:16] demultiplexer_5_out2;

  Multiplexer #(.width(4)) multiplexer_1 (.in1(4'b0000), .out(MemWriteMask), .sel(NotStore));  // open: in0
  Comparator #(.width(7)) comparator_1 (.a(Instruction[6:0]), .b(7'b0100011), .eq(SFormat));  // open: gt, lt
  Demultiplexer #(.select(3)) demultiplexer_1 (
    .out0(sb), .out1(sh), .out2(sw), .in(SFormat), .sel(Instruction[14:12]));  // open: out3, out4, out5, out6, out7
  Priority_Encoder #(.select_enc(2)) priority_encoder_1 (
    .in0(sb), .in1(sh), .in2(sw), .out(storeInstruction), .en_out(NotStore));  // open: in3, gs, en_in
  Demultiplexer #(.select(2), .width(2)) demultiplexer_2 (
    .out0(demultiplexer_2_out0), .out1(demultiplexer_2_out1), .out2(demultiplexer_2_out2),
    .in(MemAddress[1:0]), .sel(storeInstruction));  // open: out3
  Demultiplexer #(.select(2), .width(2)) demultiplexer_3 (
    .out0(demultiplexer_3_out0), .out1(demultiplexer_3_out1), .out2(demultiplexer_3_out2),
    .in(MemAddress[1:0]), .sel(storeInstruction));  // open: out3
  Demultiplexer #(.select(2), .width(8)) demultiplexer_4 (
    .out0(demultiplexer_4_out0), .out1(demultiplexer_4_out1), .out2(demultiplexer_4_out2),
    .out3(demultiplexer_4_out3), .in(DataFromReg[7:0]), .sel(demultiplexer_2_out0));
  Multiplexer #(.select(2), .width(4)) multiplexer_2 (
    .in0(4'b0001), .in1(4'b0010), .in2(4'b0100), .in3(4'b1000), .out(multiplexer_2_out),
    .sel(demultiplexer_3_out0));
  Multiplexer #(.select(2), .width(4)) multiplexer_3 (
    .in0(4'b0011), .in2(4'b1100), .out(multiplexer_3_out), .sel(demultiplexer_3_out1));  // open: in1, in3
  Multiplexer #(.select(2), .width(4)) multiplexer_4 (
    .in0(4'b1111), .out(multiplexer_4_out), .sel(demultiplexer_3_out2));  // open: in1, in2, in3
  Demultiplexer #(.select(2), .width(16)) demultiplexer_5 (
    .out0(demultiplexer_5_out0), .out2(demultiplexer_5_out2), .in(DataFromReg[15:0]),
    .sel(demultiplexer_2_out1));  // open: out1, out3
  Demultiplexer #(.select(2), .width(32)) demultiplexer_6 (
    .out0(demultiplexer_6_out0), .in(DataFromReg), .sel(demultiplexer_2_out2));  // open: out1, out2, out3
  Multiplexer #(.select(2), .width(4)) multiplexer_5 (
    .in0(multiplexer_2_out), .in1(multiplexer_3_out), .in2(multiplexer_4_out), .out(MemWriteMask),
    .sel(storeInstruction));  // open: in3
  Multiplexer #(.select(2), .width(32)) multiplexer_6 (
    .in0({{24{1'b0}}, demultiplexer_4_out0}), .in1({{16{1'b0}}, demultiplexer_4_out1, {8{1'b0}}}),
    .in2({{8{1'b0}}, demultiplexer_4_out2, {16{1'b0}}}), .in3({demultiplexer_4_out3, {24{1'b0}}}),
    .out(multiplexer_6_out), .sel(demultiplexer_2_out0));
  Multiplexer #(.select(2), .width(32)) multiplexer_7 (
    .in0({{16{1'b0}}, demultiplexer_5_out0}), .in2({demultiplexer_5_out2, {16{1'b0}}}),
    .out(multiplexer_7_out), .sel(demultiplexer_2_out1));  // open: in1, in3
  Multiplexer #(.select(2), .width(32)) multiplexer_8 (
    .in0(multiplexer_6_out), .in1(multiplexer_7_out), .in2(demultiplexer_6_out0), .out(DataToMem),
    .sel(storeInstruction));  // open: in3

  // Other names for the same wires on the sheet: opcode[6:0] = Instruction[6:0]; funct3[2:0] = Instruction[14:12];
  //   funct7[6:0] = Instruction[31:25]; lowadr[1:0] = MemAddress[1:0]

  // Notes on the sheet:
  //   INPUTS to your circuit
  //   DON'T CHANGE THE LOCATIONS OF THE INPUTS AND OUTPUTS!
  //   OUTPUT from your circuit
endmodule
