// Logisim project regfile.circ as structural Verilog: 1 circuit, main circuit regfile
module regfile (
  input  [4:0] ReadIndex1,
  input  [4:0] ReadIndex2,
  input  [4:0] WriteIndex,
  input  [31:0] WriteData,
  input  RegWEn,
  input  clk,
  output [31:0] ra,
  output [31:0] sp,
  output [31:0] t0,
  output [31:0] t1,
  output [31:0] t2,
  output [31:0] s0,
  output [31:0] s1,
  output [31:0] a0,
  output [31:0] ReadData1,
  output [31:0] ReadData2
);

  wire Reg0WEn, Reg1WEn, Reg2WEn, Reg3WEn, Reg4WEn, Reg5WEn, Reg6WEn, Reg7WEn, Reg8WEn, Reg9WEn, Reg10WEn,
       Reg11WEn, Reg12WEn, Reg13WEn, Reg14WEn, Reg15WEn, Reg16WEn, Reg17WEn, Reg18WEn, Reg19WEn, Reg20WEn,
       Reg21WEn, Reg22WEn, Reg23WEn, Reg24WEn, Reg25WEn, Reg26WEn, Reg27WEn, Reg28WEn, Reg29WEn, Reg30WEn,
       Reg31WEn;
  wire [31:0] Reg0Read, Reg1Write, Reg2Write, Reg3Read, Reg3Write, Reg4Read, Reg4Write, Reg5Write, Reg6Write,
       Reg7Write, Reg8Write, Reg9Write, Reg10Write, Reg11Read, Reg11Write, Reg12Read, Reg12Write, Reg13Read,
       Reg13Write, Reg14Read, Reg14Write, Reg15Read, Reg15Write, Reg16Read, Reg16Write, Reg17Read,
       Reg17Write, Reg18Read, Reg18Write, Reg19Read, Reg19Write, Reg20Read, Reg20Write, Reg21Read,
       Reg21Write, Reg22Read, Reg22Write, Reg23Read, Reg23Write, Reg24Read, Reg24Write, Reg25Read,
       Reg25Write, Reg26Read, Reg26Write, Reg27Read, Reg27Write, Reg28Write, Reg29Read, Reg29Write,
       Reg30Read, Reg30Write, Reg31Read, Reg31Write, Reg117Read;

  Multiplexer #(.select(5), .width(32)) multiplexer_1 (
    .in0(Reg0Read), .in1(ra), .in2(sp), .in3(Reg3Read), .in4(Reg4Read), .in5(t0), .in6(t1), .in7(t2),
    .in8(s0), .in9(s1), .in10(a0), .in11(Reg11Read), .in12(Reg12Read), .in13(Reg13Read), .in14(Reg14Read),
    .in15(Reg15Read), .in16(Reg16Read), .in17(Reg17Read), .in18(Reg18Read), .in19(Reg19Read),
    .in20(Reg20Read), .in21(Reg21Read), .in22(Reg22Read), .in23(Reg23Read), .in24(Reg24Read),
    .in25(Reg25Read), .in26(Reg26Read), .in27(Reg27Read), .in28(Reg26Read), .in29(Reg29Read),
    .in30(Reg30Read), .in31(Reg31Read), .out(ReadData1), .sel(ReadIndex1));
  Multiplexer #(.select(5), .width(32)) multiplexer_2 (
    .in0(Reg0Read), .in1(ra), .in2(sp), .in3(Reg3Read), .in4(Reg4Read), .in5(t0), .in6(t1), .in7(t2),
    .in8(s0), .in9(s1), .in10(a0), .in11(Reg11Read), .in12(Reg12Read), .in13(Reg13Read), .in14(Reg14Read),
    .in15(Reg15Read), .in16(Reg16Read), .in17(Reg17Read), .in18(Reg18Read), .in19(Reg19Read),
    .in20(Reg20Read), .in21(Reg21Read), .in22(Reg22Read), .in23(Reg23Read), .in24(Reg24Read),
    .in25(Reg25Read), .in26(Reg26Read), .in27(Reg27Read), .in28(Reg26Read), .in29(Reg29Read),
    .in30(Reg30Read), .in31(Reg31Read), .out(ReadData2), .sel(ReadIndex2));
  Demultiplexer #(.select(5), .width(32)) demultiplexer_1 (
    .out1(Reg1Write), .out2(Reg2Write), .out3(Reg3Write), .out4(Reg4Write), .out5(Reg5Write),
    .out6(Reg6Write), .out7(Reg7Write), .out8(Reg8Write), .out9(Reg9Write), .out10(Reg10Write),
    .out11(Reg11Write), .out12(Reg12Write), .out13(Reg13Write), .out14(Reg14Write), .out15(Reg15Write),
    .out16(Reg16Write), .out17(Reg17Write), .out18(Reg18Write), .out19(Reg19Write), .out20(Reg20Write),
    .out21(Reg21Write), .out22(Reg22Write), .out23(Reg23Write), .out24(Reg24Write), .out25(Reg25Write),
    .out26(Reg26Write), .out27(Reg27Write), .out28(Reg28Write), .out29(Reg29Write), .out30(Reg30Write),
    .out31(Reg31Write), .in(WriteData), .sel(WriteIndex));  // open: out0
  Register #(.width(32)) register_1 (.D({32{1'b0}}), .en(Reg0WEn), .clk(clk), .Q(Reg0Read));  // open: clr
  Register #(.width(32)) register_2 (.D(Reg1Write), .en(Reg1WEn), .clk(clk), .Q(ra));  // open: clr
  Register #(.width(32)) register_3 (.D(Reg2Write), .en(Reg2WEn), .clk(clk), .Q(sp));  // open: clr
  Register #(.width(32)) register_4 (.D(Reg3Write), .en(Reg3WEn), .clk(clk), .Q(Reg3Read));  // open: clr
  Register #(.width(32)) register_5 (.D(Reg4Write), .en(Reg4WEn), .clk(clk), .Q(Reg4Read));  // open: clr
  Register #(.width(32)) register_6 (.D(Reg5Write), .en(Reg5WEn), .clk(clk), .Q(t0));  // open: clr
  Register #(.width(32)) register_7 (.D(Reg6Write), .en(Reg6WEn), .clk(clk), .Q(t1));  // open: clr
  Register #(.width(32)) register_8 (.D(Reg7Write), .en(Reg7WEn), .clk(clk), .Q(t2));  // open: clr
  Register #(.width(32)) register_9 (.D(Reg8Write), .en(Reg8WEn), .clk(clk), .Q(s0));  // open: clr
  Register #(.width(32)) register_10 (.D(Reg9Write), .en(Reg9WEn), .clk(clk), .Q(s1));  // open: clr
  Register #(.width(32)) register_11 (.D(Reg10Write), .en(Reg10WEn), .clk(clk), .Q(a0));  // open: clr
  Register #(.width(32)) register_12 (.D(Reg11Write), .en(Reg11WEn), .clk(clk), .Q(Reg11Read));  // open: clr
  Register #(.width(32)) register_13 (.D(Reg12Write), .en(Reg12WEn), .clk(clk), .Q(Reg12Read));  // open: clr
  Register #(.width(32)) register_14 (.D(Reg13Write), .en(Reg13WEn), .clk(clk), .Q(Reg13Read));  // open: clr
  Register #(.width(32)) register_15 (.D(Reg14Write), .en(Reg14WEn), .clk(clk), .Q(Reg14Read));  // open: clr
  Register #(.width(32)) register_16 (.D(Reg15Write), .en(Reg15WEn), .clk(clk), .Q(Reg15Read));  // open: clr
  Demultiplexer #(.select(5)) demultiplexer_2 (
    .out0(Reg0WEn), .out1(Reg1WEn), .out2(Reg2WEn), .out3(Reg3WEn), .out4(Reg4WEn), .out5(Reg5WEn),
    .out6(Reg6WEn), .out7(Reg7WEn), .out8(Reg8WEn), .out9(Reg9WEn), .out10(Reg10WEn), .out11(Reg11WEn),
    .out12(Reg12WEn), .out13(Reg13WEn), .out14(Reg14WEn), .out15(Reg15WEn), .out16(Reg16WEn),
    .out17(Reg17WEn), .out18(Reg18WEn), .out19(Reg19WEn), .out20(Reg20WEn), .out21(Reg21WEn),
    .out22(Reg22WEn), .out23(Reg23WEn), .out24(Reg24WEn), .out25(Reg25WEn), .out26(Reg26WEn),
    .out27(Reg27WEn), .out28(Reg28WEn), .out29(Reg29WEn), .out30(Reg30WEn), .out31(Reg31WEn), .in(RegWEn),
    .sel(WriteIndex));
  Register #(.width(32)) register_17 (.D(Reg16Write), .en(Reg16WEn), .clk(clk), .Q(Reg16Read));  // open: clr
  Register #(.width(32)) register_18 (.D(Reg17Write), .en(Reg17WEn), .clk(clk), .Q(Reg117Read));  // open: clr
  Register #(.width(32)) register_19 (.D(Reg18Write), .en(Reg18WEn), .clk(clk), .Q(Reg18Read));  // open: clr
  Register #(.width(32)) register_20 (.D(Reg19Write), .en(Reg19WEn), .clk(clk), .Q(Reg19Read));  // open: clr
  Register #(.width(32)) register_21 (.D(Reg20Write), .en(Reg20WEn), .clk(clk), .Q(Reg20Read));  // open: clr
  Register #(.width(32)) register_22 (.D(Reg21Write), .en(Reg21WEn), .clk(clk), .Q(Reg21Read));  // open: clr
  Register #(.width(32)) register_23 (.D(Reg22Write), .en(Reg22WEn), .clk(clk), .Q(Reg22Read));  // open: clr
  Register #(.width(32)) register_24 (.D(Reg23Write), .en(Reg23WEn), .clk(clk), .Q(Reg23Read));  // open: clr
  Register #(.width(32)) register_25 (.D(Reg24Write), .en(Reg24WEn), .clk(clk), .Q(Reg24Read));  // open: clr
  Register #(.width(32)) register_26 (.D(Reg25Write), .en(Reg25WEn), .clk(clk), .Q(Reg25Read));  // open: clr
  Register #(.width(32)) register_27 (.D(Reg26Write), .en(Reg26WEn), .clk(clk), .Q(Reg26Read));  // open: clr
  Register #(.width(32)) register_28 (.D(Reg27Write), .en(Reg27WEn), .clk(clk), .Q(Reg27Read));  // open: clr
  Register #(.width(32)) register_29 (.D(Reg28Write), .en(Reg28WEn), .clk(clk), .Q(Reg26Read));  // open: clr
  Register #(.width(32)) register_30 (.D(Reg29Write), .en(Reg29WEn), .clk(clk), .Q(Reg29Read));  // open: clr
  Register #(.width(32)) register_31 (.D(Reg30Write), .en(Reg30WEn), .clk(clk), .Q(Reg30Read));  // open: clr
  Register #(.width(32)) register_32 (.D(Reg31Write), .en(Reg31WEn), .clk(clk), .Q(Reg31Read));  // open: clr

  // Other names for the same wires on the sheet: Reg1Read[31:0] = ra; Reg2Read[31:0] = sp; Reg5Read[31:0] = t0;
  //   Reg6Read[31:0] = t1; Reg7Read[31:0] = t2; Reg8Read[31:0] = s0; Reg9Read[31:0] = s1; Reg10Read[31:0] = a0;
  //   Reg28Read[31:0] = Reg26Read

  // Notes on the sheet:
  //   INPUTS to your circuit
  //   DON'T CHANGE THE LOCATIONS OF THE INPUTS AND OUTPUTS!
  //   These are DEBUG/TEST outputs from your circuit.
  //   OUTPUTS from your circuit
endmodule
