// Logisim project test-I-type-Instructions.circ as structural Verilog: 1 circuit, main circuit run_main
module run_main (
  output [31:0] ra,
  output [31:0] sp,
  output [31:0] t0,
  output [31:0] t1,
  output [31:0] t2,
  output [31:0] s0,
  output [31:0] s1,
  output [31:0] a0,
  output [31:0] RequestedAddress,
  output [31:0] RequestedInstruction,
  output [15:0] TimeStep,
  output halt
);

  wire clk;

  Clock clock_1 (.out(clk));
  // Probe on RequestedAddress
  // cpu_harness cpu_harness_1: pin names not known; wires that end beside it: RequestedInstruction, clk, RequestedAddress, ra, sp, t0, t1, t2, s0, s1, a0
  ROM #(.addrWidth(14), .dataWidth(32)) rom_1 (.addr(RequestedAddress[15:2]), .data(RequestedInstruction));
  // Probe on RequestedInstruction
  Counter #(.max('hffff), .width(16)) counter_1 (.clk(clk), .Q(TimeStep));  // open: clr, load, up, count, D, carry
  Comparator #(.width(16)) comparator_1 (.a(TimeStep), .b(16'h6f), .eq(halt));  // open: gt, lt

  // Other names for the same wires on the sheet: Instruction[31:0] = RequestedInstruction;
  //   ProgramCounter[31:0] = RequestedAddress

  // Notes on the sheet:
  //   contents of rom_1 (hex, n*v repeats v):
  //   13 413 100093 8413 200113 10413 300193 18413 400213 20413 500293 28413 600313 30413 700393 38413
  //   800413 40413 900493 48413 80413 1100893 88413 1300993 98413 1400a13 1200913 90413 a8413 1600b13
  //   b0413 1700b93 b8413 1800c13 c0413 1900c93 c8413 1a00d13 d0413 1b00d93 d8413 1c00e13 e0413 1d00e93
  //   e8413 1e00f13 f0413 1f00f93 f8413 a00513 50413 b00593 58413 c00613 60413 d00693 68413 e00713 70413
  //   f00793 78413 1000813 80413 1100893 88413 1200913 90413 1300993 98413 d0413 1b00d93 d8413 1c00e13
  //   e0413 1d00e93 e8413 1e00f13 f0413 1f00f93 f8413 a00513 50413 b00593 58413 c00613 60413 d00693 68413
  //   e00713 70413 f00793 78413 1000813 80413 1100893 88413 1200913 90413 1300993 98413 e00713 70413
  //   f00793 78413 1000813 80413 1100893 88413 1200913
  //   Instruction Memory
  //   Halts Execution After Constant # of Clock Cycles
  //   Constant
endmodule
